// Logisim project ISA.circ as structural Verilog: 2 circuits, main circuit my circuit
module my_circuit (
  input  in_1,
  input  in_2,
  input  LD_PC,
  output out_4
);

  wire [31:0] adder_1_out, PC_q;

  Adder #(.width(32)) adder_1 (.a(PC_q), .b(32'h4), .out(adder_1_out));  // open: cin, cout
  Register #(.width(32)) PC (.D(adder_1_out), .en(LD_PC), .Q(PC_q), .clk(in_1));  // open: clr

  assign out_4 = in_2;

  // Other names for the same wires on the sheet: CK = in_1
endmodule

module memory (
  input  [31:0] MAR_IN,
  input  LD_MAR,
  input  LD_MDR,
  input  in_4,
  output [31:0] out_5
);

  wire [1:0] POOP;
  wire [5:0] CRAP;
  wire [7:0] ram_1_data, ram_2_data, ram_3_data, ram_4_data;
  wire [25:2] MAR_q;

  Register #(.width(32)) MAR (.D(MAR_IN), .en(LD_MAR), .Q({CRAP, MAR_q, POOP}), .clk(in_4));  // open: clr
  RAM #(.addrWidth(24)) ram_1 (.addr(MAR_q), .data(ram_1_data), .clk(in_4), .ld(1'b1));  // open: sel, clr
  RAM #(.addrWidth(24)) ram_2 (.addr(MAR_q), .data(ram_2_data), .clk(in_4), .ld(1'b1));  // open: sel, clr
  RAM #(.addrWidth(24)) ram_3 (.addr(MAR_q), .data(ram_3_data), .clk(in_4), .ld(1'b1));  // open: sel, clr
  RAM #(.addrWidth(24)) ram_4 (.addr(MAR_q), .data(ram_4_data), .clk(in_4), .ld(1'b1));  // open: sel, clr
  Register #(.width(32)) MDR (
    .D({ram_4_data, ram_3_data, ram_2_data, ram_1_data}), .en(LD_MDR), .Q(out_5), .clk(in_4));  // open: clr

  // Other names for the same wires on the sheet: CK = in_4
endmodule
